// Logisim project Datapath.circ as structural Verilog: 6 circuits, main circuit main
module main (
  output [8:0] out_1,
  output [8:0] out_2,
  output [4:0] opcode,
  output [2:0] rd,
  output [2:0] rs,
  output [2:0] rt,
  output [13:0] out_7,
  output [13:0] out_8,
  output [13:0] out_9,
  output zero,
  output out_11,
  output [3:0] out_12,
  output [13:0] out_13,
  output [13:0] out_14
);

  wire alu_control_1_binvert, alu_control_1_cin, ALUSrc, and_1_out, Branch, clock_1_out, din, dout, MemRead,
       MemtoReg, MemWrite, PCSrc, RegDst, RegSrc, RegWrite;
  wire [2:0] multiplexer_2_out, multiplexer_3_out;
  wire [3:0] random_1_out;
  wire [8:0] adder_1_out, immaddress, register_1_q;
  wire [13:0] bit_extender_2_out, multiplexer_4_out, multiplexer_6_out, ram_1_data;

  Register #(.width(9)) register_1 (.D(out_1), .Q(register_1_q), .clk(clock_1_out));  // open: en, clr
  Clock clock_1 (.out(clock_1_out));
  Multiplexer #(.width(9)) multiplexer_1 (.in0(adder_1_out), .in1(out_2), .out(out_1), .sel(Branch));  // open: en
  Adder #(.width(9)) adder_1 (.a(9'h1), .b(register_1_q), .out(adder_1_out));  // open: cin, cout
  ROM #(.addrWidth(9), .dataWidth(14)) rom_1 (.addr(register_1_q), .data({opcode, rd, rs, rt}));  // open: sel
  assign immaddress = {{6{1'b0}}, rt};  // Bit_Extender bit_extender_1
  Multiplexer #(.width(3)) multiplexer_2 (.in0(rs), .in1(rd), .out(multiplexer_2_out), .sel(dout));  // open: en
  Multiplexer #(.width(3)) multiplexer_3 (.in0(rt), .in1(rd), .out(multiplexer_3_out), .sel(RegSrc));  // open: en
  Control_Unit control_unit_1 (
    .Opcode(opcode), .RegWrite(RegWrite), .RegDst(RegDst), .ALUSrc(ALUSrc), .MemRead(MemRead),
    .MemWrite(MemWrite), .MemtoReg(MemtoReg), .PCSrc(PCSrc), .din(din), .dout(dout), .RegSrc(RegSrc));
  Register_File register_file_1 (
    .Write_Data(multiplexer_4_out), .Read_1(out_8), .Read_2(out_13), .RD(rd), .RS(multiplexer_2_out),
    .RT(multiplexer_3_out), .Clock(clock_1_out), .Wr__enable(RegWrite));  // open: in_6
  assign bit_extender_2_out = {{11{1'b0}}, rt};  // Bit_Extender bit_extender_2
  and and_1 (and_1_out, clock_1_out, din);
  Random #(.width(4), .seed(5)) random_1 (.clk(and_1_out), .out(random_1_out));  // open: next, clr
  Multiplexer #(.width(14)) multiplexer_4 (
    .in0(multiplexer_6_out), .in1(out_14), .out(multiplexer_4_out), .sel(din));  // open: en
  assign out_14 = {{10{1'b0}}, random_1_out};  // Bit_Extender bit_extender_3
  Multiplexer #(.width(14)) multiplexer_5 (
    .in0(out_13), .in1(bit_extender_2_out), .out(out_9), .sel(ALUSrc));  // open: en
  Branch_Control branch_control_1 (
    .Opcode(opcode), .zero(zero), .PCSrc(PCSrc), .Branch(Branch), .Branch_Address(out_2),
    .immaddress(immaddress), .address({rd, rs, rt}));
  ALU_Control alu_control_1 (.Opcode(opcode), .binvert(alu_control_1_binvert), .cin(alu_control_1_cin), .ALUOp(out_12));
  _14_bit_ALU u_14_bit_alu_1 (
    .Zero(zero), .A(out_8), .B(out_9), .Cin(alu_control_1_cin), .Result(out_7),
    .Binvert(alu_control_1_binvert), .ALUOp(out_12), .Overflow(out_11));  // open: Cout
  RAM #(.addrWidth(14), .dataWidth(14), .bus("separate")) ram_1 (
    .addr(out_7), .din(out_13), .data(ram_1_data), .str(MemWrite), .clk(clock_1_out), .ld(MemRead));  // open: sel, clr
  Multiplexer #(.width(14)) multiplexer_6 (
    .in0(out_7), .in1(ram_1_data), .out(multiplexer_6_out), .sel(MemtoReg));  // open: en

  // Other names for the same wires on the sheet: address[8:0] = {rd, rs, rt}; BranchAddress[8:0] = out_2

  // Notes on the sheet:
  //   contents of rom_1 (hex, n*v repeats v):
  //   fdc 25c0 10dd 24c0 13e5 25c0 14e5 24c0 16e3 18e5 1ae2 1df3 25c0 1ff5 25c0 bfb 25c0 db4 2580 202d
  //   2300 25c0
endmodule

module Register_File (
  input  [13:0] Write_Data,
  input  [2:0] RS,
  input  [2:0] RD,
  input  Wr__enable,
  input  Clock,
  input  in_6,
  input  [2:0] RT,
  output [13:0] Read_1,
  output [13:0] Read_2
);

  wire and_1_out, and_2_out, and_3_out, and_4_out, and_5_out, and_6_out, and_7_out, and_8_out,
       decoder_1_out0, decoder_1_out1, decoder_1_out2, decoder_1_out3, decoder_1_out4, decoder_1_out5,
       decoder_1_out6, decoder_1_out7;
  wire [13:0] _001_q, _010_q, _011_q, _100_q, _101_q, _110_q, _111_q, ZERO_q;

  Decoder #(.select(3)) decoder_1 (
    .out0(decoder_1_out0), .out1(decoder_1_out1), .out2(decoder_1_out2), .out3(decoder_1_out3),
    .out4(decoder_1_out4), .out5(decoder_1_out5), .out6(decoder_1_out6), .out7(decoder_1_out7), .sel(RD));  // open: en
  and and_1 (and_1_out, decoder_1_out0, Wr__enable);
  and and_2 (and_2_out, decoder_1_out1, Wr__enable);
  and and_3 (and_3_out, decoder_1_out2, Wr__enable);
  and and_4 (and_4_out, decoder_1_out3, Wr__enable);
  and and_5 (and_5_out, decoder_1_out4, Wr__enable);
  and and_6 (and_6_out, decoder_1_out5, Wr__enable);
  and and_7 (and_7_out, decoder_1_out6, Wr__enable);
  and and_8 (and_8_out, decoder_1_out7, Wr__enable);
  Register #(.width(14)) ZERO (.D(Write_Data), .en(and_1_out), .Q(ZERO_q), .clk(Clock));  // open: clr
  Register #(.width(14)) _001 (.D(Write_Data), .en(and_2_out), .Q(_001_q), .clk(Clock));  // open: clr
  Register #(.width(14)) _010 (.en(and_3_out), .Q(_010_q), .clk(Clock));  // open: D, clr
  Register #(.width(14)) _011 (.D(Write_Data), .en(and_4_out), .Q(_011_q), .clk(Clock));  // open: clr
  Register #(.width(14)) _100 (.D(Write_Data), .en(and_5_out), .Q(_100_q), .clk(Clock));  // open: clr
  Register #(.width(14)) _101 (.D(Write_Data), .en(and_6_out), .Q(_101_q), .clk(Clock));  // open: clr
  Register #(.width(14)) _110 (.D(Write_Data), .en(and_7_out), .Q(_110_q), .clk(Clock));  // open: clr
  Register #(.width(14)) _111 (.D(Write_Data), .en(and_8_out), .Q(_111_q), .clk(Clock));  // open: clr
  Multiplexer #(.select(3), .width(14)) multiplexer_1 (
    .in0(ZERO_q), .in1(_001_q), .in2(_010_q), .in3(_011_q), .in4(_100_q), .in5(_101_q), .in6(_110_q),
    .in7(_111_q), .out(Read_1), .sel(RS), .en(in_6));
  Multiplexer #(.select(3), .width(14)) multiplexer_2 (
    .in0(ZERO_q), .in1(_001_q), .in2(_010_q), .in3(_011_q), .in4(_100_q), .in5(_101_q), .in6(_110_q),
    .in7(_111_q), .out(Read_2), .sel(RT), .en(in_6));

  // Notes on the sheet:
  //   In Assembler file(word file), we define 8 resistor.
endmodule

module _14_bit_ALU (
  input  [13:0] A,
  input  [13:0] B,
  input  Cin,
  input  Binvert,
  input  [3:0] ALUOp,
  output [13:0] Result,
  output Cout,
  output Zero,
  output Overflow
);

  wire comparator_1_lt;
  wire [3:0] bit_extender_1_out, bit_extender_2_out;
  wire [13:0] adder_1_out, and_1_out, multiplexer_1_out, multiplexer_2_out, nand_1_out, nor_1_out, not_1_out,
       or_1_out, shifter_1_out, shifter_2_out, xor_1_out;

  assign not_1_out = ~B;  // NOT_Gate not_1, 14 bits wide
  Multiplexer #(.width(14)) multiplexer_1 (
    .in0(B), .in1(not_1_out), .out(multiplexer_1_out), .sel(Binvert));  // open: en
  Bit_Extender #(.in_width(14), .out_width(4)) bit_extender_1 (.in(B), .out(bit_extender_1_out));
  Bit_Extender #(.in_width(14), .out_width(4)) bit_extender_2 (.in(B), .out(bit_extender_2_out));
  Comparator #(.width(14)) comparator_1 (.a(A), .b(B), .lt(comparator_1_lt));  // open: gt, eq
  assign and_1_out = A & B;  // AND_Gate and_1, 14 bits wide
  assign or_1_out = A | B;  // OR_Gate or_1, 14 bits wide
  assign nand_1_out = ~(A & B);  // NAND_Gate nand_1, 14 bits wide
  assign nor_1_out = ~(A | B);  // NOR_Gate nor_1, 14 bits wide
  assign xor_1_out = A ^ B;  // XOR_Gate xor_1, 14 bits wide
  Adder #(.width(14)) adder_1 (.a(A), .b(multiplexer_1_out), .out(adder_1_out), .cin(Cin), .cout(Cout));
  Shifter #(.width(14)) shifter_1 (.in(A), .\dist (bit_extender_1_out), .out(shifter_1_out));
  Shifter #(.width(14), .shift("lr")) shifter_2 (.in(A), .\dist (bit_extender_2_out), .out(shifter_2_out));
  Multiplexer #(.width(14)) multiplexer_2 (
    .in0({14{1'b0}}), .in1(14'h1), .out(multiplexer_2_out), .sel(comparator_1_lt));  // open: en
  Multiplexer #(.select(4), .width(14)) multiplexer_3 (
    .in0(and_1_out), .in1(or_1_out), .in2(nand_1_out), .in3(nor_1_out), .in4(xor_1_out), .in5(adder_1_out),
    .in6(shifter_1_out), .in7(shifter_2_out), .in8(multiplexer_2_out), .out(Result), .sel(ALUOp));  // open: in9, in10, in11, in12, in13, in14, in15, en
  nor nor_2 (Zero, Result[0], Result[1], Result[2], Result[3], Result[4], Result[5], Result[6], Result[7], Result[8], Result[9], Result[10], Result[11], Result[12], Result[13]);

  assign Overflow = Cout;

  // Notes on the sheet:
  //   Comparator = slt, slt-i
  //   In Adder = ADD, ADD-I, Sub, bne, beq, lw, sw
  //   DIN, DOUT, JUMP don't need ALU
  //   Sll
  //   Srl
  //   19 instruction Available
  //   AND
  //   OR
  //   NAND
  //   NOR
  //   X-OR
  //   Adder
  //   slt
endmodule

module Control_Unit (
  input  [4:0] Opcode,
  output din,
  output MemRead,
  output MemWrite,
  output dout,
  output MemtoReg,
  output RegWrite,
  output RegDst,
  output ALUSrc,
  output RegSrc,
  output PCSrc
);

  wire add, addi, \and , beq, bne, jump, \nand , \nor , \or , or_1_out, or_4_out, or_5_out, sll, slt, slti,
       srl, sub, \xor ;

  Decoder #(.select(5)) decoder_1 (
    .out0(\and ), .out1(\or ), .out2(\nand ), .out3(\nor ), .out4(\xor ), .out5(sll), .out6(srl), .out7(add),
    .out8(sub), .out9(addi), .out10(MemRead), .out11(MemWrite), .out12(beq), .out13(bne), .out14(slt),
    .out15(slti), .out16(jump), .out17(din), .out18(dout), .sel(Opcode));  // open: out19, out20, out21, out22, out23, out24, out25, out26, out27, out28, out29, out30, out31, en
  or or_1 (or_1_out, beq, bne);
  or or_2 (RegSrc, or_1_out, MemWrite);
  or or_3 (ALUSrc, sll, srl, addi, MemRead, MemWrite, slti);
  or or_4 (or_4_out, \xor , \and , \or , \nand , \nor , add, sub, slt);
  or or_5 (or_5_out, beq, bne);
  Priority_Encoder #(.select(1)) priority_encoder_1 (
    .in0(or_5_out), .in1(jump), .out(PCSrc));  // open: gs, en_out, en_in
  or or_6 (RegWrite, sll, srl, or_4_out, addi, MemRead, slti, din);
  or or_7 (RegDst, ALUSrc, dout);

  assign MemtoReg = MemRead;

  // Other names for the same wires on the sheet: lw = MemRead; sw = MemWrite

  // Notes on the sheet:
  //   To control RT in Resistor
  //   These Operation needs to control in ALU 2nd input
  //   These Operation needs to Write in Registor, thats why.
  //   For jump
  //   DIN = Data  In
  //   DOUT = Data Out
  //   to enter any data in resistor
  //   to see resistor value in output
endmodule

module ALU_Control (
  input  [4:0] Opcode,
  output binvert,
  output cin,
  output [3:0] ALUOp
);

  wire add, addi, \and , beq, bne, din, dout, jump, lw, \nand , \nor , \or , or_1_out, or_2_out, sll, slt,
       slti, srl, sub, sw, \xor ;

  Decoder #(.select(5)) decoder_1 (
    .out0(\and ), .out1(\or ), .out2(\nand ), .out3(\nor ), .out4(\xor ), .out5(sll), .out6(srl), .out7(add),
    .out8(sub), .out9(addi), .out10(lw), .out11(sw), .out12(beq), .out13(bne), .out14(slt), .out15(slti),
    .out16(jump), .out17(din), .out18(dout), .sel(Opcode));  // open: out19, out20, out21, out22, out23, out24, out25, out26, out27, out28, out29, out30, out31, en
  or or_1 (or_1_out, add, sub, addi, bne, lw, sw, beq);
  or or_2 (or_2_out, slt, slti);
  or or_3 (binvert, beq, bne, sub);
  Priority_Encoder #(.select(4)) priority_encoder_1 (
    .in0(\and ), .in1(\or ), .in2(\nand ), .in3(\nor ), .in4(\xor ), .in5(or_1_out), .in6(sll), .in7(srl),
    .in8(or_2_out), .out(ALUOp));  // open: in9, in10, in11, in12, in13, in14, in15, gs, en_out, en_in

  assign cin = binvert;

  // Notes on the sheet:
  //   We use the same thing but for ALU Control, We use Priority Encoder
  //   To perform Sub, beq, bne in Adder, we have to use 2's compliment.
  //   In 14-bit ALU, we create seperate line and some line added with adder to perform operation using 1 Pin.
endmodule

module Branch_Control (
  input  [4:0] Opcode,
  input  zero,
  input  [8:0] immaddress,
  input  [8:0] address,
  input  PCSrc,
  output Branch,
  output [8:0] Branch_Address
);

  wire add, addi, \and , and_1_out, and_2_out, beq, bne, din, dout, jump, lw, \nand , \nor , not_1_out, \or ,
       sll, slt, slti, srl, sub, sw, \xor ;

  Decoder #(.select(5)) decoder_1 (
    .out0(\and ), .out1(\or ), .out2(\nand ), .out3(\nor ), .out4(\xor ), .out5(sll), .out6(srl), .out7(add),
    .out8(sub), .out9(addi), .out10(lw), .out11(sw), .out12(beq), .out13(bne), .out14(slt), .out15(slti),
    .out16(jump), .out17(din), .out18(dout), .sel(Opcode));  // open: out19, out20, out21, out22, out23, out24, out25, out26, out27, out28, out29, out30, out31, en
  not not_1 (not_1_out, zero);
  and and_1 (and_1_out, beq, zero);
  and and_2 (and_2_out, bne, not_1_out);
  Multiplexer #(.width(9)) multiplexer_1 (
    .in0(immaddress), .in1(address), .out(Branch_Address), .sel(PCSrc));  // open: en
  or or_1 (Branch, and_1_out, and_2_out, jump);

  // Notes on the sheet:
  //   address =
  //   immaddress = immediate number
  //   Zero = Zero signal from ALU
  //   Branch = Mux Select Bit
  //   PCSrc = Comes from control unit for Jump
  //   Jump number(how many instruction you have to jump)
  //   BEQ, BNE & Jump needs to jump instruction, thats why they were connected.
  //   Branch Address = Sending Jump instruction to Instruction fetch, for Next Instruction
endmodule
